# Fritzing sketch led_only (saved by Fritzing 0.8.7b)
breadboards: 1

parts:
  BeagleBone1 = BeagleBone Black
  R1 = Resistor [tolerance=±5% resistance=100 package=THT]
  LED1 = smd LED [color="Red (633nm)" package="0603 [SMD]"]

nets:
  N1: BeagleBone1.no_name_yet#1, LED1.cathode
  N2: BeagleBone1.no_name_yet#11, R1.Pin_0
  N3: R1.Pin_1, LED1.anode

custom parts:
  BeagleBone Black: BeagleBone Black rev. A5B
