# Fritzing sketch motion_sensor (saved by Fritzing 0.8.7b)

parts:
  BeagleBone1 = BeagleBone Black
  Part1 = HC-SR501 Body Sensor Module

nets:
  N1: BeagleBone1.no_name_yet#1, Part1.VCC
  N2: BeagleBone1.no_name_yet#3, Part1.GND
  N3: BeagleBone1.no_name_yet#12, Part1.OUT

custom parts:
  BeagleBone Black: BeagleBone Black rev. A5B
  HC-SR501 Body Sensor Module: Pyroelectric Infrared PIR Motion Sensor Detector Module
