# Fritzing sketch temp_sensor (saved by Fritzing 0.8.7b)
breadboards: 1

parts:
  BeagleBone1 = BeagleBone Black
  T1 = TMP36 Temperature Sensor [package="TO92 [THT]"]

nets:
  N1: BeagleBone1.no_name_yet#1, T1.GND
  N2: BeagleBone1.no_name_yet#3, T1.+Vs
  N3: BeagleBone1.no_name_yet#40, T1.Vout

custom parts:
  BeagleBone Black: BeagleBone Black rev. A5B
